# Fritzing sketch BME280 (saved by Fritzing 1.0.0rc)

parts:
  M1 = BME280
  U1 = JST XH 4A 2.54mm [package=THT]

nets:
  N1: M1.VIN, U1.pin1
  N2: M1.GND, U1.pin2
  N3: M1.SCL, U1.pin3
  N4: M1.SDA, U1.pin4

custom parts:
  BME280: Temperature Humidity Barometric presure Sensor
  JST XH 4A 2.54mm: 4 Pin JST XH connector
