# Fritzing sketch UV-Module (saved by Fritzing 1.0.0rc)

parts:
  U8 = JST XH 3A Male [chip_label=? package=THT]
  Bauteil3 = Ambient Light Sensor (TEMT6000 Breakout Board)

nets:
  N1: U8.pin1, Bauteil3.S
  N2: U8.pin2, Bauteil3.GND
  N3: U8.pin3, Bauteil3.VCC

custom parts:
  JST XH 3A Male: 2.54 Mm JST "XH" connector
