# Fritzing sketch Datenzwerg (saved by Fritzing 1.0.0rc)
circuit board: 7.98761cm x 6.67983cm
breadboards: 1

parts:
  U3 = JST XH 3A Male [chip_label=? package=THT]
  U4 = JST XH 3A Male [chip_label=? package=THT]
  U5 = JST XH 4A 2.54mm [package=THT]
  Bauteil1 = Adafruit ADS1115 16Bit I2C ADC [part_number="Adafruit #1085"]
  U8 = JST XH 3A Male [chip_label=? package=THT]
  U6 = JST XH 3A Male [chip_label=? package=THT]
  Bauteil3 = Ambient Light Sensor (TEMT6000 Breakout Board)
  U10 = LM2596 step down module
  U7 = JST XH 3A Male [chip_label=? package=THT]
  TP1 = TP4056 [chip_label=TP4056 package="DIP (Dual Inline) [THT]"]
  Bauteil2 = Breakout Board for Electret Microphone
  M1 = BME280
  U1 = JST XH 4A 2.54mm [package=THT]
  BAT1 = 18650 battery holder [package=battery-18650-kit]
  WeMos_D1_Mini1 = WeMos D1 Mini
  U11 = JST XH 3A Male [chip_label=? package=THT]

nets:
  N1: U3.pin1, Bauteil1.AIN1
  N2: U3.pin2, U4.pin2, U5.pin3, Bauteil1.GND, U11.pin2
  N3: U3.pin3, Bauteil1.VDD
  N4: U4.pin1, Bauteil1.AIN0
  N5: U5.pin1, Bauteil1.SDA
  N6: U5.pin2, Bauteil1.SCL
  N7: U5.pin4, WeMos_D1_Mini1.D6
  N8: U8.pin1, Bauteil3.S
  N9: U8.pin2, Bauteil3.GND
  N10: U8.pin3, Bauteil3.VCC
  N11: U6.pin1, Bauteil2.AUD
  N12: U6.pin2, Bauteil2.GND
  N13: U6.pin3, Bauteil2.VCC
  N14: U10.IN+, U7.pin1, TP1.pin3
  N15: U10.IN-, U10.OUT-, U7.pin2, TP1.pin6
  N16: U10.OUT+, U7.pin3
  N17: TP1.pin4, BAT1.+
  N18: TP1.pin5, BAT1.-
  N19: M1.VIN, U1.pin4
  N20: M1.GND, U1.pin3
  N21: M1.SCL, U1.pin2
  N22: M1.SDA, U1.pin1
  N23: WeMos_D1_Mini1.A0, U11.pin1
  N24: WeMos_D1_Mini1.D0, WeMos_D1_Mini1.RST

custom parts:
  JST XH 3A Male: 2.54 Mm JST "XH" connector
  JST XH 4A 2.54mm: 4 Pin JST XH connector
  Adafruit ADS1115 16Bit I2C ADC: For microcontrollers without an analog-to-digital converter or when you want a higher-precision ADC, the ADS1115 provides 16-bit precision at 860 samples/second over I2C. The chip can be configured as 4 single-ended input channels, or two differential channels. As a nice bonus, it even includes a programmable gain amplifier, up to x16, to help boost up smaller single/differential signals to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
  LM2596 step down module: LM2596 DC-DC step down power supply module 3 A.
  TP4056: A DIP stand-in part for whatever IC you want. With 6 pins on a 300mil dual inline package (DIP) footprint.
  BME280: Temperature Humidity Barometric presure Sensor
  18650 battery holder: 18650 Battery Holder
