# Fritzing sketch Power-module (saved by Fritzing 1.0.0rc)

parts:
  M1 = RioRand LM2596
  BAT1 = 18650 battery holder [package=battery-18650-kit]
  TP1 = TP4056 [chip_label=TP4056 package="DIP (Dual Inline) [THT]"]
  U1 = JST XH 3A Male [chip_label=? package=THT]

nets:
  N1: M1.Pin_1, TP1.pin3, U1.pin1
  N2: M1.Pin_2, TP1.pin6
  N3: M1.Pin_3, U1.pin2
  N4: M1.Pin_4, U1.pin3
  N5: BAT1.+, TP1.pin4
  N6: BAT1.-, TP1.pin5

custom parts:
  18650 battery holder: 18650 Battery Holder
  TP4056: A DIP stand-in part for whatever IC you want. With 6 pins on a 300mil dual inline package (DIP) footprint.
  JST XH 3A Male: 2.54 Mm JST "XH" connector
