# Fritzing sketch sound module (saved by Fritzing 1.0.0rc)

parts:
  U6 = JST XH 3A Male [chip_label=? package=THT]
  Bauteil2 = Breakout Board for Electret Microphone

nets:
  N1: U6.pin1, Bauteil2.AUD
  N2: U6.pin2, Bauteil2.GND
  N3: U6.pin3, Bauteil2.VCC

custom parts:
  JST XH 3A Male: 2.54 Mm JST "XH" connector
